// Logisim project Test.circ as structural Verilog: 1 circuit, main circuit main
module main (
);

  wire clock_1_out, lvc16373_1_p2, lvc16373_1_p9, lvc16373_1_p10;
  wire [7:0] counter_1_q;

  Clock clock_1 (.out(clock_1_out));
  Random random_1 ();  // open: clk, next, out, clr
  Counter counter_1 (.Q(counter_1_q), .clk(clock_1_out));  // open: load, D, count, carry, up, clr
  // LVC16373 lvc16373_1: pin names not known; wires that end beside it: clock_1_out, lvc16373_1_p2, counter_1_q[1], lvc16373_1_p2, counter_1_q[2], counter_1_q[1], lvc16373_1_p2, counter_1_q[3], lvc16373_1_p9, lvc16373_1_p10
  // Probe on lvc16373_1_p9
  // Probe on lvc16373_1_p10
endmodule
